// Digital circuit 01_DR_EX.dig as structural Verilog
module _01_DR_EX (
  input  [31:0] IW_1,
  input  [31:0] RD0_1,
  input  [31:0] RD1_1,
  input  CLK,
  input  EN,
  input  CLR,
  input  [1:0] EXT_1,
  input  ALUB_1,
  input  [2:0] ALUO_1,
  input  MR_1,
  input  MW_1,
  input  [3:0] WR_1,
  input  WDsl_1,
  input  RFW_1,
  input  [1:0] PCsl_1,
  input  [31:0] PC4_1,
  input  [3:0] RR0,
  input  [3:0] RR1,
  output [31:0] IW_2,
  output [31:0] RD0_2,
  output [31:0] RD1_2,
  output [1:0] EXT_2,
  output ALUB_2,
  output [2:0] ALUO_2,
  output MR_2,
  output MW_2,
  output [3:0] WR_2,
  output WDsl_2,
  output RFW_2,
  output [1:0] PCsl_2,
  output [31:0] PC4_2,
  output [3:0] RR0_2,
  output [3:0] RR1_2
);

  // register_clr_32bits register_clr_32bits_1: pin names not known; wires that end beside it: IW_1, CLK, EN, CLR, IW_2
  // register_clr_32bits register_clr_32bits_2: pin names not known; wires that end beside it: RD0_1, CLK, EN, CLR, RD0_2
  // register_clr_32bits register_clr_32bits_3: pin names not known; wires that end beside it: RD1_1, CLK, EN, CLR, RD1_2
  // register_clr_2bits register_clr_2bits_1: pin names not known; wires that end beside it: EXT_1, CLK, EN, CLR, EXT_2
  // register_clr_1bit register_clr_1bit_1: pin names not known; wires that end beside it: ALUB_1, CLK, EN, CLR, ALUB_2
  // register_clr_3bits register_clr_3bits_1: pin names not known; wires that end beside it: ALUO_1, CLK, EN, CLR, ALUO_2
  // register_clr_1bit register_clr_1bit_2: pin names not known; wires that end beside it: MR_1, CLK, EN, CLR, MR_2
  // register_clr_1bit register_clr_1bit_3: pin names not known; wires that end beside it: MW_1, CLK, EN, CLR, MW_2
  // register_clr_4bits register_clr_4bits_1: pin names not known; wires that end beside it: WR_1, CLK, EN, CLR, WR_2
  // register_clr_1bit register_clr_1bit_4: pin names not known; wires that end beside it: WDsl_1, CLK, EN, CLR, WDsl_2
  // register_clr_1bit register_clr_1bit_5: pin names not known; wires that end beside it: RFW_1, CLK, EN, CLR, RFW_2
  // register_clr_2bits register_clr_2bits_2: pin names not known; wires that end beside it: PCsl_1, CLK, EN, CLR, PCsl_2
  // register_clr_32bits register_clr_32bits_4: pin names not known; wires that end beside it: PC4_1, CLK, EN, CLR, PC4_2
  // register_clr_4bits register_clr_4bits_2: pin names not known; wires that end beside it: RR0, CLK, EN, CLR, RR0_2
  // register_clr_4bits register_clr_4bits_3: pin names not known; wires that end beside it: RR1, CLK, EN, CLR, RR1_2
endmodule
