// Digital circuit project07.dig as structural Verilog
module project07 (
  input  CLK,
  input  CLR,
  input  [2:0] PROG,
  output DONE,
  output [31:0] R0
);

  wire a_mul, alu_1_p4, ALUB_1, ALUB_2, C, CLK_t, decode_ascii_1_p2, decode_ascii_1_p3, decode_ascii_1_p4,
       decode_ascii_1_p5, decode_ascii_2_p3, decode_ascii_2_p4, decode_ascii_2_p5, decode_ascii_2_p6,
       decode_ascii_3_p2, decode_ascii_3_p3, decode_ascii_3_p4, decode_ascii_3_p5, decode_ascii_4_p4,
       decode_ascii_4_p5, decode_ascii_4_p6, decode_ascii_4_p7, decode_ascii_5_p6, decode_ascii_5_p7,
       decode_ascii_5_p8, decode_ascii_5_p9, i_dp, instruction_memory_1_p7, IW_3, MR_1, MR_2, MR_3, MR_4,
       MW_1, MW_2, MW_3, N, not_1_out, PC4_3, PCsl_3, r1, r2, r3, r4, r5, r6, r7, r8, r9, r10, r11, r12, r13,
       r14, r15, RFW_1, RFW_2, RFW_3, RFW_4, RR1sl_1, V, WDsl_1, WDsl_2, WDsl_3, WDsl_4, WRsl_1, Z;
  wire [1:0] EXT_1, EXT_2, PCsl_1, PCsl_2, PCsl_4, RR0sl_1, SEL0, SEL1;
  wire [2:0] ALUO_1, ALUO_2;
  wire [3:0] cond, RR0_1, RR0_2, RR1_1, RR1_2, WR_1, WR_2, WR_3, WR_4;
  wire [23:0] b_offset;
  wire [27:24] IW_0;
  wire [31:0] _00_if_dr_1_p4, _01_dr_ex_1_rd1_2, _02_ex_mem_1_p11, _03_mem_wb_1_p12, a, add_1_s, b,
       decode_ascii_5_p4, extension_unit_1_p3, instruction_memory_1_p4, IW_1, IW_2, IW_4, multiplexer_5_out,
       multiplexer_6_out, multiplexer_7_out, multiplexer_8_out, multiplexer_9_out, PC4_2, RAM_d, RD0_2,
       register_clr_32bits_1_p1, register_clr_32bits_1_p5, register_file_clr_1_p9, register_file_clr_1_p10;

  // Probe on {cond, IW_0[27:26], i_dp, IW_0[24], b_offset[23:22], a_mul, b_offset[20:0]}
  and and_1 (CLK_t, CLK, ~DONE);  // And
  // register_clr_32bits register_clr_32bits_1: pin names not known; wires that end beside it: register_clr_32bits_1_p1, CLK_t, 1'b1, CLR, register_clr_32bits_1_p5
  Multiplexer #(.Selector_Bits(2), .Bits(32)) multiplexer_1 (
    .sel(PCsl_4), .in_0(add_1_s), .in_1(multiplexer_9_out), .in_2(_01_dr_ex_1_rd1_2), .in_3({32{1'b0}}),
    .out(register_clr_32bits_1_p1));
  // Probe on decode_ascii_1_p2
  // Probe on decode_ascii_1_p3
  // decode_ascii decode_ascii_1: pin names not known; wires that end beside it: {cond, IW_0[27:26], i_dp, IW_0[24], b_offset[23:22], a_mul, b_offset[20:0]}, decode_ascii_1_p2, decode_ascii_1_p3, decode_ascii_1_p4, decode_ascii_1_p5
  Add #(.Bits(32)) add_1 (.a(register_clr_32bits_1_p5), .b(32'h4), .c_i(1'b0), .s(add_1_s));  // open: c_o
  // Probe on decode_ascii_1_p4
  // Probe on decode_ascii_1_p5
  // instruction_memory instruction_memory_1: pin names not known; wires that end beside it: register_clr_32bits_1_p5[8:2], PROG, {cond, IW_0[27:26], i_dp, IW_0[24], b_offset[23:22], a_mul, b_offset[20:0]}, instruction_memory_1_p4, CLK_t, 1'b1, instruction_memory_1_p7
  Add #(.Bits(32)) add_2 (.a(add_1_s), .b(32'h4), .c_i(1'b0), .s(instruction_memory_1_p4));  // open: c_o
  // Probe on R0
  // Probe on r1
  // Probe on r2
  // Probe on r3
  // Probe on cond
  // Probe on cond
  // Probe on cond
  // Probe on cond
  // _00_IF_DR _00_if_dr_1: pin names not known; wires that end beside it: {cond, IW_0[27:26], i_dp, IW_0[24], b_offset[23:22], a_mul, b_offset[20:0]}, add_1_s, IW_1, _00_if_dr_1_p4
  // Probe on r4
  // Probe on r5
  // Probe on r6
  // Probe on r7
  // Probe on IW_0[27:26]
  // Probe on {IW_0[27:26], i_dp, IW_0[24], b_offset[23]}
  // Probe on IW_0[27:26]
  // Probe on {IW_0[27:26], i_dp}
  // Probe on i_dp
  // Probe on i_dp
  // Probe on IW_0[24]
  // decode_ascii decode_ascii_2: pin names not known; wires that end beside it: CLR, IW_1, decode_ascii_2_p3, decode_ascii_2_p4, decode_ascii_2_p5, decode_ascii_2_p6
  // Probe on {IW_0[24], b_offset[23:22], a_mul}
  // Probe on a_mul
  // Probe on IW_0[24]
  // Probe on decode_ascii_2_p3
  // Probe on decode_ascii_2_p4
  // Probe on r8
  // Probe on r9
  // Probe on r10
  // Probe on r11
  // Probe on b_offset[20]
  // Probe on b_offset[23]
  // Probe on {b_offset[23:22], a_mul, b_offset[20:0]}
  Multiplexer #(.Selector_Bits(2), .Bits(4)) multiplexer_2 (
    .sel(RR0sl_1), .in_0(IW_1[19:16]), .in_1(4'b1111), .in_2(4'b0000), .in_3(4'b0000), .out(RR0_1));
  Multiplexer #(.Bits(4)) multiplexer_3 (.sel(RR1sl_1), .in_0(IW_1[3:0]), .in_1(IW_1[19:16]), .out(RR1_1));
  Multiplexer #(.Bits(4)) multiplexer_4 (.sel(WRsl_1), .in_0(IW_1[15:12]), .in_1(4'b1110), .out(WR_1));
  Multiplexer #(.Bits(32)) multiplexer_5 (
    .sel(WDsl_4), .in_0(multiplexer_9_out), .in_1(decode_ascii_5_p4), .out(multiplexer_5_out));
  // Probe on decode_ascii_2_p5
  // Probe on decode_ascii_2_p6
  // Probe on b_offset[20]
  // Probe on b_offset[19:16]
  // Probe on b_offset[22]
  // decoder decoder_1: pin names not known; wires that end beside it: IW_1, RFW_1, EXT_1, ALUB_1, ALUO_1, PCsl_1, RR0sl_1, RR1sl_1, WRsl_1, WDsl_1, MR_1, MW_1
  not not_1 (not_1_out, CLK_t);
  // Probe on b_offset[19:16]
  // Probe on b_offset[15:12]
  // Probe on a_mul
  // register_file_clr register_file_clr_1: pin names not known; wires that end beside it: RR0_1, RR1_1, WR_4, multiplexer_5_out, RFW_4, instruction_memory_1_p7, not_1_out, CLR, register_file_clr_1_p9, register_file_clr_1_p10, R0, r1, r2, r3, r4, r5, r6, r7, r8, r9, r10, r11, r12, r13, r14, r15
  // Probe on r12
  // Probe on r13
  // Probe on r14
  // Probe on r15
  // Probe on b_offset[15:12]
  // Probe on b_offset[11:8]
  // Probe on b_offset[20]
  // Probe on b_offset[3:0]
  // Probe on b_offset[7:0]
  // Probe on b_offset[19:16]
  // Probe on N
  // Probe on Z
  // Probe on C
  // Probe on V
  // Probe on b_offset[7:4]
  // Probe on b_offset[15:12]
  // Probe on b_offset[3:0]
  // Probe on b_offset[3:0]
  // Probe on b_offset[11:0]
  _01_DR_EX _01_dr_ex_1 (
    .IW_1(IW_1), .RD0_1(register_file_clr_1_p9), .RD1_1(register_file_clr_1_p10), .EXT_1(EXT_1),
    .ALUB_1(ALUB_1), .ALUO_1(ALUO_1), .MR_1(MR_1), .MW_1(MW_1), .WR_1(WR_1), .WDsl_1(WDsl_1), .RFW_1(RFW_1),
    .PCsl_1(PCsl_1), .PC4_1(_00_if_dr_1_p4), .RR0(RR0_1), .RR1(RR1_1), .IW_2(IW_2), .RD0_2(RD0_2),
    .RD1_2(_01_dr_ex_1_rd1_2), .EXT_2(EXT_2), .ALUB_2(ALUB_2), .ALUO_2(ALUO_2), .MR_2(MR_2), .MW_2(MW_2),
    .WR_2(WR_2), .WDsl_2(WDsl_2), .RFW_2(RFW_2), .PCsl_2(PCsl_2), .PC4_2(PC4_2), .RR0_2(RR0_2),
    .RR1_2(RR1_2), .CLK(CLK_t), .EN(1'b1), .CLR(CLR));
  Comparator #(.Bits(32)) comparator_1 (.a(IW_4), .b(32'he2800000), .eq(DONE));  // open: gt, lt
  // Probe on decode_ascii_3_p2
  // decode_ascii decode_ascii_3: pin names not known; wires that end beside it: IW_2, decode_ascii_3_p2, decode_ascii_3_p3, decode_ascii_3_p4, decode_ascii_3_p5
  hazard_unit hazard_unit_1 (
    .RR0_2(RR0_2), .WR_2(WR_2), .RFW_2(RFW_2), .RR1_2(RR1_2), .WR_3(WR_3), .RFW_3(RFW_3), .WR_4(WR_4),
    .RFW_4(RFW_4), .SEL0(SEL0), .SEL1(SEL1));
  // Probe on decode_ascii_3_p3
  // Probe on decode_ascii_3_p4
  Multiplexer #(.Selector_Bits(2), .Bits(32)) multiplexer_6 (
    .sel(SEL1), .in_0(_01_dr_ex_1_rd1_2), .in_1(a), .in_2(b), .in_3({32{1'b0}}), .out(multiplexer_6_out));
  // Probe on decode_ascii_3_p5
  Multiplexer #(.Selector_Bits(2), .Bits(32)) multiplexer_7 (
    .sel(SEL0), .in_0(RD0_2), .in_1(a), .in_2(b), .in_3({32{1'b0}}), .out(multiplexer_7_out));
  Multiplexer #(.Bits(32)) multiplexer_8 (
    .sel(ALUB_2), .in_0(multiplexer_6_out), .in_1(extension_unit_1_p3), .out(multiplexer_8_out));
  // extension_unit extension_unit_1: pin names not known; wires that end beside it: IW_2, EXT_2, extension_unit_1_p3, PCsl_2, PC4_2, CLK_t, PCsl_3, PC4_3
  // alu alu_1: pin names not known; wires that end beside it: multiplexer_7_out, multiplexer_8_out, ALUO_2, alu_1_p4, N, Z, C, V
  // Probe on extension_unit_1_p3
  // _02_EX_MEM _02_ex_mem_1: pin names not known; wires that end beside it: IW_2, alu_1_p4, _01_dr_ex_1_rd1_2, MR_2, MW_2, WR_2, WDsl_2, RFW_2, IW_3, b, _02_ex_mem_1_p11, MR_3, MW_3, WR_3, WDsl_3, RFW_3
  // decode_ascii decode_ascii_4: pin names not known; wires that end beside it: 1'b1, CLR, IW_3, decode_ascii_4_p4, decode_ascii_4_p5, decode_ascii_4_p6, decode_ascii_4_p7
  // Probe on decode_ascii_4_p4
  // Probe on decode_ascii_4_p5
  // Probe on decode_ascii_4_p6
  // Probe on decode_ascii_4_p7
  RAMDualPort #(.AddrBits(8), .Bits(32)) RAM (
    .A(b[9:2]), .Din(_02_ex_mem_1_p11), .str(MW_3), .C(CLK_t), .ld(MR_3), .D(RAM_d));
  // _03_MEM_WB _03_mem_wb_1: pin names not known; wires that end beside it: IW_3, b, RAM_d, MR_3, WR_3, WDsl_3, RFW_3, PCsl_3, PC4_3, IW_4, a, _03_mem_wb_1_p12, MR_4, WR_4, WDsl_4, RFW_4
  // Probe on decode_ascii_5_p6
  // decode_ascii decode_ascii_5: pin names not known; wires that end beside it: CLK_t, 1'b1, CLR, decode_ascii_5_p4, IW_4, decode_ascii_5_p6, decode_ascii_5_p7, decode_ascii_5_p8, decode_ascii_5_p9
  // Probe on decode_ascii_5_p7
  // Probe on decode_ascii_5_p8
  // Probe on decode_ascii_5_p9
  Multiplexer #(.Bits(32)) multiplexer_9 (.sel(MR_4), .in_0(a), .in_1(_03_mem_wb_1_p12), .out(multiplexer_9_out));

  // Other names for the same wires on the sheet: imm[7:0] = b_offset[7:0]; immoff[11:0] = b_offset[11:0];
  //   IW_0 (some bits) = {cond, i_dp, b_offset[23:22], a_mul, b_offset[20:0]}; rm[3:0] = b_offset[3:0];
  //   rm_mul[3:0] = b_offset[3:0]; opmul4[3:0] = b_offset[7:4]; rs_mul[3:0] = b_offset[11:8];
  //   rd[3:0] = b_offset[15:12]; rn_mul[3:0] = b_offset[15:12]; rd_mul[3:0] = b_offset[19:16];
  //   rn[3:0] = b_offset[19:16]; l_sdt = b_offset[20]; s_dp = b_offset[20]; s_mul = b_offset[20];
  //   b_offset[21] = a_mul; opc[3:0] = {IW_0[24], b_offset[23:22], a_mul}; w_sdt = a_mul; b_sdt = b_offset[22];
  //   opmul6[4:0] = {IW_0[27:26], i_dp, IW_0[24], b_offset[23]}; u_sdt = b_offset[23]; l_b = IW_0[24];
  //   p_sdt = IW_0[24]; i_sdt = i_dp; opb3[2:0] = {IW_0[27:26], i_dp}; op2[1:0] = IW_0[27:26];
  //   opmul2[1:0] = IW_0[27:26]

  // Notes on the sheet:
  //   DP
  //   MUL
  //   SDT
  //   B
  //   SP
  //   LR
  //   PC
endmodule
